# Fritzing sketch 28BYJ48 (saved by Fritzing 0.9.5d)

parts:
  Part1 = Arduino Mega ADK (Rev3)
  MOTOR1 = 28BYJ-48 Stepper Motor
  BREAKOUT1 = ULN2003A breakout board

nets:
  5V: Part1.5V, BREAKOUT1.+5V
  N1: Part1.GND, BREAKOUT1.0V
  N2: Part1.D4_PWM, BREAKOUT1.In_1
  N3: Part1.D5_PWM, BREAKOUT1.In_2
  N4: Part1.D6_PWM, BREAKOUT1.In_3
  N5: Part1.D7_PWM, BREAKOUT1.In_4
  N6: MOTOR1.BLUE, BREAKOUT1.BLUE_wire
  N7: MOTOR1.PINK, BREAKOUT1.PINK_wire
  N8: MOTOR1.RED, BREAKOUT1.RED_wire
  N9: MOTOR1.ORANGE, BREAKOUT1.ORANGE_wire
  N10: MOTOR1.YELLOW, BREAKOUT1.YELLOW_wire

notes:
  12V DC

custom parts:
  28BYJ-48 Stepper Motor: 28BYJ-48 gear-reduction stepper motor (small)
  ULN2003A breakout board: ULN2003A 7-way Darlington Transistor Driver on breakoutboard
