# Fritzing sketch IR and limit switch (saved by Fritzing 0.9.5d)

parts:
  M1 = fc-51 [package=THT]
  Part1 = Arduino Mega ADK (Rev3)
  M2 = fc-51 [package=THT]
  JL012-13-5_1 = JL012-13-5.2 Lever (Limit) Switch SPDT + NO + NC [part_number=JL012-13-5.2]
  R1 = Resistor [tolerance=±5% resistance=10000 package="2512 [SMD]"]

nets:
  N1: M1.pin1, Part1.D39
  N2: M1.pin2, M2.pin2
  N3: M1.pin3, M2.pin3
  N4: Part1.5V, JL012-13-5_1.C
  N5: Part1.D41, M2.pin1
  N6: Part1.GND, R1.Pin_0
  N7: JL012-13-5_1.NO, R1.Pin_1

notes:
  12V DC

custom parts:
  JL012-13-5.2 Lever (Limit) Switch SPDT + NO + NC: Micro Switch; Model No.: JL012-13.5-2; Actuator Action: Momentary; Actuator Type: Hinge Lever; Contact Configuration: 1NO, 1NC (SPDT) Temperature -25~65℃；Relative humidity: below 85%; Rate Voltage: 125V AC; Rated Current: 1A.
