# Fritzing sketch Keypad and display (saved by Fritzing 0.9.5d)

parts:
  Part1 = Arduino Mega ADK (Rev3)
  Display1 = LCD screen 16x2 IIC [part_number=101290]
  Part2 = 4x4 Keypad [part_number=101207]

nets:
  N1: Part1.D21/SCL, Display1.SCL
  N2: Part1.D20/SDA, Display1.SDA
  5V: Part1.5V, Display1.VCC
  GND: Part1.GND, Display1.GND
  N3: Part1.D31, Part2.1
  N4: Part1.D32, Part2.2
  N5: Part1.D33, Part2.3
  N6: Part1.D34, Part2.4
  N7: Part1.D35, Part2.5
  N8: Part1.D36, Part2.6
  N9: Part1.D37, Part2.7
  N10: Part1.D38, Part2.8

notes:
  12V DC

custom parts:
  LCD screen 16x2 IIC: LCD screen with HD44780 controller enables showing text, symbols, value or anything else that comes from Croduino/Arduino. It is capable of showing 16 symbols in two lines and therefore can be used in many projects that need to send clearly visible and legible output information.. • Color of symbols: White • Backlight: Blue • Dimensions: 80 x 36 x 12 mm • Screen dimensions: 64.5 x 16 mm •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
  4x4 Keypad: Matrix membrane keypad 4x4
