# Fritzing sketch Wiper motor with relay (saved by Fritzing 0.9.5d)

parts:
  Part1 = Arduino Mega ADK (Rev3)
  KY-1 = Keyes Relay [package=THT]
  M2 = DC Motor

nets:
  N1: Part1.5V, KY-1.power
  N2: Part1.GND, KY-1.ground
  N3: Part1.D30, KY-1.signal
  N4: KY-1.NO, M2.pin_1

notes:
  12V DC

custom parts:
  Keyes Relay: The Keyes 5V relay module is suitable for SCM development, home appliance control. It uses a 5V~12V TIL control signal which can control DC / AC signal.
