# Fritzing sketch buzzer (saved by Fritzing 0.9.5d)

parts:
  SG1 = Buzzer 12mm [package=buzzer-ccv]
  Part1 = Arduino Mega ADK (Rev3)

nets:
  N1: SG1.1, Part1.D44
  N2: SG1.2, Part1.GND

notes:
  12V DC
