# Fritzing sketch main (saved by Fritzing 0.9.5d)

parts:
  Part1 = Arduino Mega ADK (Rev3)
  Pololu_A1 = Pololu A4988 [package=SO16]
  Pololu_A2 = Pololu A4988 [package=SO16]
  Pololu_A3 = Pololu A4988 [package=SO16]
  Pololu_A4 = Pololu A4988 [package=SO16]
  BREAKOUT1 = ULN2003A breakout board
  J1 = Piezo Speaker
  M1 = fc-51 [package=THT]
  M2 = fc-51 [package=THT]
  M3 = Stepper Motor - Bipolar
  M4 = Stepper Motor - Bipolar
  M5 = Stepper Motor - Bipolar
  M6 = Stepper Motor - Bipolar
  MOTOR1 = 28BYJ-48 Stepper Motor
  BREAKOUT2 = ULN2003A breakout board
  MOTOR2 = 28BYJ-48 Stepper Motor
  JL012-13-5_1 = JL012-13-5.2 Lever (Limit) Switch SPDT + NO + NC [part_number=JL012-13-5.2]
  M7 = DC Motor
  S1 = H-Bridge with L298N
  M8 = DC Motor
  Mod1 = KY-019 5V Relay Module [package="Breakout board"]
  R1 = Resistor [tolerance=±5% resistance=10000 package="0402 [SMD]"]
  C1 = Capacitor Polarized [package=panasonic_c]
  C2 = Capacitor Polarized [package=panasonic_c]
  C3 = Capacitor Polarized [package=panasonic_c]
  C4 = Capacitor Polarized [package=panasonic_c]
  KEYPAD = 4x4 Keypad [part_number=101207]
  LCD_I2C = LCD screen 16x2 IIC [part_number=101290]
  J2 = Camdenboss CTB0158-3 [part_number=CTB0158-3 package=THT]

nets:
  N1: Part1.D21/SCL, LCD_I2C.SCL
  N2: Part1.D20/SDA, LCD_I2C.SDA
  N3: Part1.D19/RX1, BREAKOUT2.In_4
  N4: Part1.D18/TX1, BREAKOUT2.In_3
  N5: Part1.D17/RX2, BREAKOUT2.In_2
  N6: Part1.D16/TX2, BREAKOUT2.In_1
  N7: Part1.GND, J2.terminal_3
  N8: Part1.D11_PWM, Pololu_A2.DIR
  N9: Part1.D10_PWM, Pololu_A2.STEP
  N10: Part1.VIN, J2.terminal_1
  N11: Part1.D4_PWM, BREAKOUT1.In_1
  N12: Part1.D5_PWM, BREAKOUT1.In_2
  N13: Part1.D6_PWM, BREAKOUT1.In_3
  N14: Part1.D7_PWM, BREAKOUT1.In_4
  N15: Part1.D24, S1.IN1
  N16: Part1.D25, S1.IN2
  N17: Part1.D26, Pololu_A1.STEP
  N18: Part1.D27, Pololu_A1.DIR
  N19: Part1.D28, Pololu_A3.STEP, Pololu_A4.STEP
  N20: Part1.D29, Pololu_A3.DIR, Pololu_A4.DIR
  N21: Part1.D30, Mod1.S
  N22: Part1.D31, KEYPAD.1
  N23: Part1.D32, KEYPAD.2
  N24: Part1.D33, KEYPAD.3
  N25: Part1.D34, KEYPAD.4
  N26: Part1.D35, KEYPAD.5
  N27: Part1.D36, KEYPAD.6
  N28: Part1.D37, KEYPAD.7
  N29: Part1.D38, KEYPAD.8
  N30: Part1.D39, M1.pin1
  N31: Part1.D40, JL012-13-5_1.NO, R1.Pin_1
  N32: Part1.D41, M2.pin1
  N33: Part1.D44, J1.pin1
  N34: Pololu_A1.RESET, Pololu_A1.SLEEP
  N35: Pololu_A1.GND#8, Pololu_A2.GND#8, Pololu_A3.GND#8, Pololu_A4.GND#8, J1.pin2, Mod1.-, R1.Pin_0, LCD_I2C.GND
  VDD: Pololu_A1.VDD, Pololu_A2.VDD, Pololu_A3.VDD, Pololu_A4.VDD, JL012-13-5_1.C, Mod1.+, LCD_I2C.VCC, J2.terminal_2
  N36: Pololu_A1.1B, M3.D
  N37: Pololu_A1.1A, M3.B
  N38: Pololu_A1.2A, M3.C
  N39: Pololu_A1.2B, M3.A
  N40: Pololu_A1.GND#14, Pololu_A2.GND#14, Pololu_A3.GND#14, Pololu_A4.GND#14, S1.GND, M8.pin_2, C1.-, C2.-, C3.-, C4.-
  N41: Pololu_A1.VMOT, Pololu_A2.VMOT, Pololu_A3.VMOT, Pololu_A4.VMOT, S1.12V, Mod1.Common, C1.+, C2.+, C3.+, C4.+
  N42: Pololu_A2.RESET, Pololu_A2.SLEEP
  N43: Pololu_A2.1B, M6.D
  N44: Pololu_A2.1A, M6.B
  N45: Pololu_A2.2A, M6.C
  N46: Pololu_A2.2B, M6.A
  N47: Pololu_A3.RESET, Pololu_A3.SLEEP
  N48: Pololu_A3.1B, M4.D
  N49: Pololu_A3.1A, M4.B
  N50: Pololu_A3.2A, M4.C
  N51: Pololu_A3.2B, M4.A
  N52: Pololu_A4.RESET, Pololu_A4.SLEEP
  N53: Pololu_A4.1B, M5.D
  N54: Pololu_A4.1A, M5.B
  N55: Pololu_A4.2A, M5.C
  N56: Pololu_A4.2B, M5.A
  N57: BREAKOUT1.0V, BREAKOUT2.0V
  +5V: BREAKOUT1.+5V, BREAKOUT2.+5V
  N58: BREAKOUT1.RED_wire, MOTOR1.RED
  N59: BREAKOUT1.ORANGE_wire, MOTOR1.ORANGE
  N60: BREAKOUT1.YELLOW_wire, MOTOR1.YELLOW
  N61: BREAKOUT1.PINK_wire, MOTOR1.PINK
  N62: BREAKOUT1.BLUE_wire, MOTOR1.BLUE
  N63: M1.pin2, M2.pin2
  N64: M1.pin3, M2.pin3
  N65: BREAKOUT2.RED_wire, MOTOR2.RED
  N66: BREAKOUT2.ORANGE_wire, MOTOR2.ORANGE
  N67: BREAKOUT2.YELLOW_wire, MOTOR2.YELLOW
  N68: BREAKOUT2.PINK_wire, MOTOR2.PINK
  N69: BREAKOUT2.BLUE_wire, MOTOR2.BLUE
  N70: M7.pin_1, S1.MB2
  N71: M7.pin_2, S1.MB1
  N72: M8.pin_1, Mod1.NO

notes:
  +12V
  GND
  +5V

custom parts:
  ULN2003A breakout board: ULN2003A 7-way Darlington Transistor Driver on breakoutboard
  28BYJ-48 Stepper Motor: 28BYJ-48 gear-reduction stepper motor (small)
  JL012-13-5.2 Lever (Limit) Switch SPDT + NO + NC: Micro Switch; Model No.: JL012-13.5-2; Actuator Action: Momentary; Actuator Type: Hinge Lever; Contact Configuration: 1NO, 1NC (SPDT) Temperature -25~65℃；Relative humidity: below 85%; Rate Voltage: 125V AC; Rated Current: 1A.
  H-Bridge with L298N: h-bridge
  KY-019 5V Relay Module: KY-019 5V Relay module, used to control AC circuits. (Special thanks to vanepp for fixing the PCB holes and other errors)
  4x4 Keypad: Matrix membrane keypad 4x4
  LCD screen 16x2 IIC: LCD screen with HD44780 controller enables showing text, symbols, value or anything else that comes from Croduino/Arduino. It is capable of showing 16 symbols in two lines and therefore can be used in many projects that need to send clearly visible and legible output information.. • Color of symbols: White • Backlight: Blue • Dimensions: 80 x 36 x 12 mm • Screen dimensions: 64.5 x 16 mm •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
