# Fritzing sketch nema 17 with a4988 (saved by Fritzing 0.9.5d)

parts:
  Part1 = Arduino Mega ADK (Rev3)
  Pololu_A1 = Pololu A4988 [package=SO16]
  M2 = Stepper Motor - Bipolar  # not connected

nets:
  N1: Part1.D11_PWM, Pololu_A1.DIR
  N2: Part1.D10_PWM, Pololu_A1.STEP
  N3: Pololu_A1.RESET, Pololu_A1.SLEEP

notes:
  12V DC
  5V DC
